# Fritzing sketch RP2040 + MAX30102 Schmatics - Healthcare Telemetry (saved by Fritzing 0.9.3b)
circuit board: 8.46667cm x 5.64444cm
breadboards: 1

parts:
  M1 = Arduino Nano 33 IOT-tht
  M2 = MakerFocus MAX30102

nets:
  N1: M1.pin_8, M2.SDA
  N2: M1.pin_9, M2.SCL
  N3: M1.pin_13, M1.pin_18
  N4: M1.pin_14, M1.pin_19, M2.GND

custom parts:
  Arduino Nano 33 IOT-tht: The Arduino Nano 33 IoT is the easiest and cheapest point of entry to enhance existing devices (and creating new ones) to be part of the IoT and designing pico-network applications. Whether you are looking at building a sensor network connected to your office or home router, or if you want to create a BLE device sending data to a cellphone, the Nano 33 IoT is your one-stop-solution for many of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
  MakerFocus MAX30102: Oximeter module using the MAX30102 chip. As usual, if you want the mounting holes in pcb, you need to drag a hole over the pad in silkscreen to actually drill the hole (by default they are not drilled)
